// Logisim project digital4 (2).circ as structural Verilog: 1 circuit, main circuit main
module main (
  output [3:0] out_1
);

  wire and_1_out, and_2_out, and_3_out, and_4_out, and_5_out, and_6_out, and_7_out, button_1_out,
       button_2_out, button_3_out, clock_1_out, d_ff_1_q, d_ff_2_q, d_ff_3_q, d_ff_4_q, d_ff_5_q, d_ff_6_q,
       d_ff_7_q, d_ff_8_q, d_ff_9_q, d_ff_9_qn, d_ff_10_q, not_1_out, not_2_out, not_3_out, not_4_out,
       not_5_out, not_6_out, not_7_out, or_1_out, or_2_out, or_3_out, or_4_out, or_5_out, or_6_out, or_7_out,
       reset_out, xor_1_out;
  wire [3:0] counter_2_q;

  Button button_1 (.out(button_1_out));
  Button button_2 (.out(button_2_out));
  Button button_3 (.out(button_3_out));
  not not_1 (not_1_out, or_7_out);
  not not_2 (not_2_out, or_7_out);
  not not_3 (not_3_out, or_7_out);
  D_Flip_Flop d_ff_1 (.D(not_4_out), .clk(not_4_out), .Q(d_ff_1_q), .reset(not_1_out));  // open: Qn, preset
  not not_4 (not_4_out, d_ff_10_q);
  and and_1 (and_1_out, button_2_out, not_2_out);
  not not_5 (not_5_out, or_7_out);
  and and_2 (and_2_out, button_1_out, not_3_out);
  or or_1 (or_1_out, d_ff_1_q, reset_out);
  Clock clock_1 (.out(clock_1_out));
  and and_3 (and_3_out, button_3_out, not_5_out);
  Counter #(.max('hf), .width(4)) counter_1 (
    .clr(or_1_out), .clk(d_ff_9_q), .Q(out_1));  // open: load, up, count, D, carry
  Counter #(.max('hf), .width(4)) counter_2 (
    .clr(or_4_out), .clk(and_4_out), .Q(counter_2_q));  // open: load, up, count, D, carry
  and and_4 (and_4_out, and_6_out, clock_1_out);
  D_Flip_Flop d_ff_2 (.D(and_3_out), .clk(and_3_out), .Q(d_ff_2_q), .reset(or_7_out));  // open: Qn, preset
  D_Flip_Flop d_ff_3 (.D(d_ff_2_q), .clk(and_1_out), .Q(d_ff_3_q), .reset(or_6_out));  // open: Qn, preset
  or or_2 (or_2_out, and_1_out, and_3_out, and_2_out);
  or or_3 (or_3_out, and_1_out, and_3_out);
  D_Flip_Flop d_ff_4 (.D(d_ff_9_qn), .clk(or_2_out), .Q(d_ff_4_q), .reset(d_ff_7_q));  // open: Qn, preset
  not not_6 (not_6_out, counter_2_q[0]);
  not not_7 (not_7_out, counter_2_q[2]);
  D_Flip_Flop d_ff_5 (.D(d_ff_3_q), .clk(or_3_out), .Q(d_ff_5_q));  // open: Qn, preset, reset
  D_Flip_Flop d_ff_6 (.D(d_ff_3_q), .clk(and_2_out), .Q(d_ff_6_q), .reset(reset_out));  // open: Qn, preset
  and and_5 (and_5_out, d_ff_3_q, and_2_out);
  D_Flip_Flop d_ff_7 (.D(d_ff_4_q), .clk(or_2_out), .Q(d_ff_7_q), .reset(d_ff_9_q));  // open: Qn, preset
  and and_6 (and_6_out, out_1[0], out_1[1]);
  D_Flip_Flop d_ff_8 (.D(and_6_out), .clk(and_6_out), .Q(d_ff_8_q), .reset(or_4_out));  // open: Qn, preset
  or or_4 (or_4_out, and_7_out, reset_out);
  and and_7 (and_7_out, not_6_out, counter_2_q[1], not_7_out, counter_2_q[3]);
  D_Flip_Flop d_ff_9 (.D(d_ff_7_q), .clk(xor_1_out), .Q(d_ff_9_q), .Qn(d_ff_9_qn), .reset(d_ff_9_q));  // open: preset
  xor xor_1 (xor_1_out, or_2_out, and_5_out);
  D_Flip_Flop d_ff_10 (.D(d_ff_8_q), .clk(d_ff_8_q), .Q(d_ff_10_q), .reset(or_5_out));  // open: Qn, preset
  or or_5 (or_5_out, and_7_out, reset_out);
  LED KEY (.in(d_ff_6_q));
  Hex_Digit_Display hex_digit_display_1 (.value(out_1));  // open: dp
  // Digital_Oscilloscope digital_oscilloscope_1: pin names not known
  or or_6 (or_6_out, d_ff_5_q, reset_out);
  Button reset (.out(reset_out));
  LED LOCKOUT (.in(d_ff_10_q));
  or or_7 (or_7_out, reset_out, d_ff_10_q);

  // Notes on the sheet:
  //   A
  //   B
  //   C
  //   B A C
  //   WRONG
endmodule
